// Logisim project ROM_message_spitter.circ as structural Verilog: 1 circuit, main circuit main
module main (
  input  trigger,
  input  clock,
  input  reset,
  output [6:0] \output 
);

  wire or_1_out;
  wire [10:0] counter_1_q;

  or or_1 (or_1_out, trigger, \output [0], \output [1], \output [2], \output [3], \output [4], \output [5], \output [6]);
  Counter #(.width(11), .max('h7ff)) counter_1 (
    .count(or_1_out), .Q(counter_1_q), .clk(clock), .clr(reset));  // open: load, D, carry
  ROM #(.addrWidth(11), .dataWidth(7)) rom_1 (.addr(counter_1_q), .data(\output ));  // open: sel

  // Notes on the sheet:
  //   start jakwidzi zero to sie zatrzymuje 
  //   komunikaty
  //   contents of rom_1 (hex, n*v repeats v):
  //   0 47 72 61 20 6e 69 65 20 6d 61 20 6e 61 20 63 65 6c 75 20 6f 62 72 61 7a 61 6e 69 61 20 69 20 7a 6e
  //   69 65 73 6c 61 77 69 61 6e 69 61 20 6a 61 6b 69 65 6a 6b 6f 6c 77 69 65 6b 20 6f 73 6f 62 79 2c 20
  //   69 6e 73 74 79 74 75 63 6a 69 20 6c 75 62 20 50 72 6f 66 2e 20 64 72 2e 20 68 61 62 2e 20 69 6e 7a
  //   2e 0 4a 65 73 74 65 73 20 7a 77 79 6b 6c 79 6d 20 70 72 6f 66 65 73 6f 72 65 6d 20 6a 61 6b 69 63 68
  //   20 77 69 65 6c 75 2e 0 50 6f 6b 61 7a 75 6a 65 73 7a 20 73 74 75 64 65 6e 74 6f 6d 20 77 79 63 69 61
  //   67 20 7a 20 72 65 67 75 6c 61 6d 69 6e 75 20 73 74 75 64 69 6f 77 2e 0 5a 61 6b 61 7a 75 6a 65 73 7a
  //   20 70 69 73 61 63 20 64 6f 20 73 69 65 62 69 65 20 65 2d 6d 61 69 6c 65 2e 0 47 72 6f 7a 69 73 7a 20
  //   73 74 75 64 65 6e 74 6f 6d 20 70 72 6f 63 65 73 65 6d 20 7a 61 20 66 61 6c 73 7a 6f 77 61 6e 69 65
  //   20 70 6f 64 70 69 73 6f 77 2e 0 53 74 75 64 65 6e 63 69 20 7a 61 63 7a 79 6e 61 6a 61 20 73 69 65 20
  //   6e 69 65 70 6f 6b 6f 69 63 20 69 6c 6f 73 63 69 61 20 69 20 73 7a 79 62 6b 6f 73 63 69 61 20 6f 6d
  //   61 77 69 61 6e 65 67 6f 20 6d 61 74 65 72 69 61 6c 75 2e 0 50 72 7a 65 72 61 62 69 61 73 7a 20 70 69
  //   65 72 77 73 7a 65 20 32 30 20 73 6c 61 6a 64 6f 77 2c 20 61 20 6e 61 73 74 65 70 6e 65 20 38 30 20
  //   70 72 7a 65 6b 6c 69 6b 75 6a 65 73 7a 2e 0 50 6f 6a 61 77 69 61 6a 61 20 73 69 65 20 70 69 65 72 77
  //   73 7a 65 20 67 6c 6f 73 79 20 6b 72 79 74 79 6b 69 20 6e 61 20 74 77 6f 6a 20 74 65 6d 61 74 2e 0 53
  //   74 75 64 65 6e 63 69 20 6e 69 65 20 77 69 65 64 7a 61 20 63 6f 20 64 7a 69 65 6a 65 20 73 69 65 20
  //   6e 61 20 77 79 6b 6c 61 64 7a 69 65 2e 0 50 6f 64 65 6a 72 7a 65 77 61 73 7a 2c 20 7a 65 20 74 77 6f
  //   69 20 64 6f 6b 74 6f 72 7a 79 20 70 72 6f 62 75 6a 61 20 63 68 72 6f 6e 69 63 20 73 74 75 64 65 6e
  //   74 6f 77 20 70 72 7a 65 64 20 74 6f 62 61 2e 0 4e 61 20 77 79 6b 6c 61 64 7a 69 65 20 6b 74 6f 73 20
  //   6b 72 7a 79 6b 6e 61 6c 20 27 63 6f 20 63 69 20 7a 72 6f 62 69 6c 65 6d 20 74 79 20 63 2a 2a 2a 75
  //   27 2e 0 50 74 61 6b 69 20 70 72 7a 65 73 74 61 6a 61 20 63 77 69 65 72 6b 61 63 20 6b 69 65 64 79 20
  //   77 79 63 68 6f 64 7a 69 73 7a 20 7a 20 62 75 64 79 6e 6b 75 2e 0 50 72 7a 65 64 20 74 77 6f 69 6d 20
  //   67 61 62 69 6e 65 74 65 6d 20 66 75 6e 6b 63 6a 6f 6e 75 6a 65 20 73 74 61 6c 79 20 6b 6f 6d 69 74
  //   65 74 20 6b 6f 6c 65 6a 6b 6f 77 79 2e 0 4b 61 64 72 61 20 6e 61 75 6b 6f 77 61 20 6d 61 20 63 69 65
  //   20 7a 61 20 64 7a 69 77 61 6b 61 2e 0 53 74 75 64 65 6e 63 69 20 73 7a 75 6b 61 6a 61 20 73 70 6f 73
  //   6f 62 6f 77 20 6e 61 20 74 77 6f 6a 20 65 67 7a 61 6d 69 6e 2e 0 54 77 6f 6a 65 20 6e 61 7a 77 69 73
  //   6b 6f 20 6a 65 73 74 20 6e 61 20 77 79 64 7a 69 61 6c 65 20 73 79 6e 6f 6e 69 6d 65 6d 20 77 61 72
  //   75 6e 6b 75 2e 0 50 72 7a 65 73 74 61 6a 65 73 7a 20 7a 77 72 61 63 61 63 20 75 77 61 67 65 20 63 6f
  //   20 70 69 73 7a 65 73 7a 20 6e 61 20 74 61 62 6c 69 63 79 2e 0 50 6f 77 74 61 72 7a 61 6e 69 65 20 74
  //   77 6f 6a 65 67 6f 20 70 72 7a 65 64 6d 69 6f 74 75 20 6f 66 69 63 6a 61 6c 6e 69 65 20 77 70 69 73
  //   61 6e 6f 20 64 6f 20 70 6c 61 6e 75 20 73 74 75 64 69 6f 77 2e 0 50 6f 77 73 74 61 6a 65 20 77 79 64
  //   7a 69 61 6c 6f 77 79 20 74 65 6c 65 66 6f 6e 20 7a 61 75 66 61 6e 69 61 20 64 6c 61 20 74 77 6f 69
  //   63 68 20 6f 66 69 61 72 2e 0 55 41 4d 20 6f 74 77 69 65 72 61 20 6b 69 65 72 75 6e 65 6b 20 41 75 74
  //   6f 6d 61 74 79 6b 61 20 69 20 52 6f 62 6f 74 79 6b 61 20 64 6c 61 20 75 63 68 6f 64 7a 63 6f 77 20
  //   7a 20 50 6f 6c 69 74 65 63 68 6e 69 6b 69 2e 0 55 77 61 6c 69 6c 65 73 20 6e 61 6a 77 69 65 63 65 6a
  //   20 73 74 75 64 65 6e 74 6f 77 20 77 20 68 69 73 74 6f 72 69 69 20 75 63 7a 65 6c 6e 69 20 6a 65 73
  //   7a 63 7a 65 20 70 72 7a 65 64 20 73 65 73 6a 61 2e 0 57 79 6b 6c 61 64 6f 77 63 79 20 7a 20 4b 6f 72
  //   65 69 20 50 6f 6c 6e 6f 63 6e 65 6a 20 70 72 7a 79 6a 65 7a 64 7a 61 6a 61 20 70 6f 64 67 6c 61 64
  //   61 63 20 74 77 6f 6a 65 20 6d 65 74 6f 64 79 2e 0 53 72 65 64 6e 69 61 20 77 69 65 6b 75 20 6e 61 20
  //   31 20 72 6f 6b 75 20 74 6f 20 33 35 20 6c 61 74 2e 0 5a 72 6f 7a 70 61 63 7a 65 6e 69 20 72 6f 64 7a
  //   69 63 65 20 73 74 75 64 65 6e 74 6f 77 20 62 6c 61 67 61 6a 61 20 7a 65 62 79 73 20 6f 64 7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
endmodule
