// Logisim project comparator_score_thresholds.circ as structural Verilog: 1 circuit, main circuit main
module main (
  input  [15:0] score,
  input  clk,
  input  reset,
  output [15:0] out,
  output pulse
);

  wire comparator_1_gt, not_1_out;
  wire [4:0] counter_1_q;

  Counter #(.width(5), .max('h1f)) counter_1 (
    .Q(counter_1_q), .clk(pulse), .clr(reset));  // open: load, D, count, carry
  Multiplexer #(.select(5), .width(16), .enable("false")) multiplexer_1 (
    .in0(16'h1), .in1(16'h32), .in2(16'h64), .in3(16'hc8), .in4(16'hfa), .in5(16'h12c), .in6(16'h15e),
    .in7(16'h190), .in8(16'h1c2), .in9(16'h1f4), .in10(16'h226), .in11(16'h258), .in12(16'h28a),
    .in13(16'h2bc), .in14(16'h2ee), .in15(16'h320), .in16(16'h352), .in17(16'h384), .in18(16'h3b6),
    .in19(16'h3e8), .in20(16'h44c), .in21(16'h4b0), .in22(16'h514), .in23(16'h578), .in24(16'h5dc),
    .in25(16'h640), .in26(16'h6a4), .in27(16'h708), .in28(16'h76c), .in29(16'h7d0), .in30(16'h9c4),
    .in31(16'hbb8), .out(out), .sel(counter_1_q));
  not not_1 (not_1_out, comparator_1_gt);
  Comparator #(.width(16), .mode("unsigned")) comparator_1 (.a(out), .b(score), .gt(comparator_1_gt));  // open: eq, lt
  D_Flip_Flop d_ff_1 (.clk(clk), .D(not_1_out), .Q(pulse));  // open: Qn, preset, en, reset
endmodule
