// Logisim project display_buffer.circ as structural Verilog: 1 circuit, main circuit main
module main (
  input  [31:0] Address,
  input  [4:0] Select,
  output Done,
  output [31:0] out_4,
  output [31:0] out_5,
  output [31:0] out_6,
  output [31:0] out_7,
  output [31:0] out_8,
  output [31:0] out_9,
  output [31:0] out_10,
  output [31:0] out_11,
  output [31:0] out_12,
  output [31:0] out_13,
  output [31:0] out_14,
  output [31:0] out_15,
  output [31:0] out_16,
  output [31:0] out_17,
  output [31:0] out_18,
  output [31:0] out_19,
  output [31:0] out_20,
  output [31:0] out_21,
  output [31:0] out_22,
  output [31:0] out_23,
  output [31:0] out_24,
  output [31:0] out_25,
  output [31:0] out_26,
  output [31:0] out_27,
  output [31:0] out_28,
  output [31:0] out_29,
  output [31:0] out_30,
  output [31:0] out_31,
  output [31:0] out_32,
  output [31:0] out_33,
  output [31:0] out_34,
  output [31:0] out_35
);

  wire demultiplexer_1_out1, demultiplexer_1_out2, demultiplexer_1_out3, demultiplexer_1_out4,
       demultiplexer_1_out5, demultiplexer_1_out6, demultiplexer_1_out7, demultiplexer_1_out8,
       demultiplexer_1_out9, demultiplexer_1_out10, demultiplexer_1_out11, demultiplexer_1_out12,
       demultiplexer_1_out13, demultiplexer_1_out14, demultiplexer_1_out15, demultiplexer_1_out16,
       demultiplexer_1_out17, demultiplexer_1_out18, demultiplexer_1_out19, demultiplexer_1_out20,
       demultiplexer_1_out21, demultiplexer_1_out22, demultiplexer_1_out23, demultiplexer_1_out24,
       demultiplexer_1_out25, demultiplexer_1_out26, demultiplexer_1_out27, demultiplexer_1_out28,
       demultiplexer_1_out29, demultiplexer_1_out30, demultiplexer_1_out31;
  wire [31:0] register_1_q, register_2_q, register_3_q, register_4_q, register_5_q, register_6_q,
       register_7_q, register_8_q, register_9_q, register_10_q, register_11_q, register_12_q, register_13_q,
       register_14_q, register_15_q, register_16_q, register_17_q, register_18_q, register_19_q,
       register_20_q, register_21_q, register_22_q, register_23_q, register_24_q, register_25_q,
       register_26_q, register_27_q, register_28_q, register_29_q, register_30_q, register_31_q,
       register_32_q;

  Demultiplexer #(.select(5), .enable("false")) demultiplexer_1 (
    .out0(Done), .out1(demultiplexer_1_out1), .out2(demultiplexer_1_out2), .out3(demultiplexer_1_out3),
    .out4(demultiplexer_1_out4), .out5(demultiplexer_1_out5), .out6(demultiplexer_1_out6),
    .out7(demultiplexer_1_out7), .out8(demultiplexer_1_out8), .out9(demultiplexer_1_out9),
    .out10(demultiplexer_1_out10), .out11(demultiplexer_1_out11), .out12(demultiplexer_1_out12),
    .out13(demultiplexer_1_out13), .out14(demultiplexer_1_out14), .out15(demultiplexer_1_out15),
    .out16(demultiplexer_1_out16), .out17(demultiplexer_1_out17), .out18(demultiplexer_1_out18),
    .out19(demultiplexer_1_out19), .out20(demultiplexer_1_out20), .out21(demultiplexer_1_out21),
    .out22(demultiplexer_1_out22), .out23(demultiplexer_1_out23), .out24(demultiplexer_1_out24),
    .out25(demultiplexer_1_out25), .out26(demultiplexer_1_out26), .out27(demultiplexer_1_out27),
    .out28(demultiplexer_1_out28), .out29(demultiplexer_1_out29), .out30(demultiplexer_1_out30),
    .out31(demultiplexer_1_out31), .in(1'b1), .sel(Select));
  Register #(.width(32), .trigger("falling")) register_1 (.D(Address), .Q(register_1_q), .clk(Done));  // open: en, clr
  Register #(.width(32), .trigger("falling")) register_2 (
    .D(Address), .Q(register_2_q), .clk(demultiplexer_1_out1));  // open: en, clr
  Register #(.width(32), .trigger("falling")) register_3 (
    .D(Address), .Q(register_3_q), .clk(demultiplexer_1_out2));  // open: en, clr
  Register #(.width(32), .trigger("falling")) register_4 (
    .D(Address), .Q(register_4_q), .clk(demultiplexer_1_out3));  // open: en, clr
  Register #(.width(32), .trigger("falling")) register_5 (
    .D(Address), .Q(register_5_q), .clk(demultiplexer_1_out4));  // open: en, clr
  Register #(.width(32), .trigger("falling")) register_6 (
    .D(Address), .Q(register_6_q), .clk(demultiplexer_1_out5));  // open: en, clr
  Register #(.width(32), .trigger("falling")) register_7 (
    .D(Address), .Q(register_7_q), .clk(demultiplexer_1_out6));  // open: en, clr
  Register #(.width(32), .trigger("falling")) register_8 (
    .D(Address), .Q(register_8_q), .clk(demultiplexer_1_out7));  // open: en, clr
  Register #(.width(32), .trigger("falling")) register_9 (
    .D(Address), .Q(register_9_q), .clk(demultiplexer_1_out8));  // open: en, clr
  Register #(.width(32), .trigger("falling")) register_10 (
    .D(Address), .Q(register_10_q), .clk(demultiplexer_1_out9));  // open: en, clr
  Register #(.width(32), .trigger("falling")) register_11 (
    .D(Address), .Q(register_11_q), .clk(demultiplexer_1_out10));  // open: en, clr
  Register #(.width(32), .trigger("falling")) register_12 (
    .D(Address), .Q(register_12_q), .clk(demultiplexer_1_out11));  // open: en, clr
  Register #(.width(32), .trigger("falling")) register_13 (
    .D(Address), .Q(register_13_q), .clk(demultiplexer_1_out12));  // open: en, clr
  Register #(.width(32), .trigger("falling")) register_14 (
    .D(Address), .Q(register_14_q), .clk(demultiplexer_1_out13));  // open: en, clr
  Register #(.width(32), .trigger("falling")) register_15 (
    .D(Address), .Q(register_15_q), .clk(demultiplexer_1_out14));  // open: en, clr
  Register #(.width(32), .trigger("falling")) register_16 (
    .D(Address), .Q(register_16_q), .clk(demultiplexer_1_out15));  // open: en, clr
  Register #(.width(32), .trigger("falling")) register_17 (
    .D(Address), .Q(register_17_q), .clk(demultiplexer_1_out16));  // open: en, clr
  Register #(.width(32), .trigger("falling")) register_18 (
    .D(Address), .Q(register_18_q), .clk(demultiplexer_1_out17));  // open: en, clr
  Register #(.width(32), .trigger("falling")) register_19 (
    .D(Address), .Q(register_19_q), .clk(demultiplexer_1_out18));  // open: en, clr
  Register #(.width(32), .trigger("falling")) register_20 (
    .D(Address), .Q(register_20_q), .clk(demultiplexer_1_out19));  // open: en, clr
  Register #(.width(32), .trigger("falling")) register_21 (
    .D(Address), .Q(register_21_q), .clk(demultiplexer_1_out20));  // open: en, clr
  Register #(.width(32), .trigger("falling")) register_22 (
    .D(Address), .Q(register_22_q), .clk(demultiplexer_1_out21));  // open: en, clr
  Register #(.width(32), .trigger("falling")) register_23 (
    .D(Address), .Q(register_23_q), .clk(demultiplexer_1_out22));  // open: en, clr
  Register #(.width(32), .trigger("falling")) register_24 (
    .D(Address), .Q(register_24_q), .clk(demultiplexer_1_out23));  // open: en, clr
  Register #(.width(32), .trigger("falling")) register_25 (
    .D(Address), .Q(register_25_q), .clk(demultiplexer_1_out24));  // open: en, clr
  Register #(.width(32), .trigger("falling")) register_26 (
    .D(Address), .Q(register_26_q), .clk(demultiplexer_1_out25));  // open: en, clr
  Register #(.width(32), .trigger("falling")) register_27 (
    .D(Address), .Q(register_27_q), .clk(demultiplexer_1_out26));  // open: en, clr
  Register #(.width(32), .trigger("falling")) register_28 (
    .D(Address), .Q(register_28_q), .clk(demultiplexer_1_out27));  // open: en, clr
  Register #(.width(32), .trigger("falling")) register_29 (
    .D(Address), .Q(register_29_q), .clk(demultiplexer_1_out28));  // open: en, clr
  Register #(.width(32), .trigger("falling")) register_30 (
    .D(Address), .Q(register_30_q), .clk(demultiplexer_1_out29));  // open: en, clr
  Register #(.width(32), .trigger("falling")) register_31 (
    .D(Address), .Q(register_31_q), .clk(demultiplexer_1_out30));  // open: en, clr
  Register #(.width(32), .trigger("falling")) register_32 (
    .D(Address), .Q(register_32_q), .clk(demultiplexer_1_out31));  // open: en, clr
  Register #(.width(32), .trigger("falling")) register_33 (.D(register_1_q), .Q(out_4), .clk(Done));  // open: en, clr
  Register #(.width(32), .trigger("falling")) register_34 (.D(register_2_q), .Q(out_5), .clk(Done));  // open: en, clr
  Register #(.width(32), .trigger("falling")) register_35 (.D(register_3_q), .Q(out_6), .clk(Done));  // open: en, clr
  Register #(.width(32), .trigger("falling")) register_36 (.D(register_4_q), .Q(out_7), .clk(Done));  // open: en, clr
  Register #(.width(32), .trigger("falling")) register_37 (.D(register_5_q), .Q(out_8), .clk(Done));  // open: en, clr
  Register #(.width(32), .trigger("falling")) register_38 (.D(register_6_q), .Q(out_9), .clk(Done));  // open: en, clr
  Register #(.width(32), .trigger("falling")) register_39 (.D(register_7_q), .Q(out_10), .clk(Done));  // open: en, clr
  Register #(.width(32), .trigger("falling")) register_40 (.D(register_8_q), .Q(out_11), .clk(Done));  // open: en, clr
  Register #(.width(32), .trigger("falling")) register_41 (.D(register_9_q), .Q(out_12), .clk(Done));  // open: en, clr
  Register #(.width(32), .trigger("falling")) register_42 (.D(register_10_q), .Q(out_13), .clk(Done));  // open: en, clr
  Register #(.width(32), .trigger("falling")) register_43 (.D(register_11_q), .Q(out_14), .clk(Done));  // open: en, clr
  Register #(.width(32), .trigger("falling")) register_44 (.D(register_12_q), .Q(out_15), .clk(Done));  // open: en, clr
  Register #(.width(32), .trigger("falling")) register_45 (.D(register_13_q), .Q(out_16), .clk(Done));  // open: en, clr
  Register #(.width(32), .trigger("falling")) register_46 (.D(register_14_q), .Q(out_17), .clk(Done));  // open: en, clr
  Register #(.width(32), .trigger("falling")) register_47 (.D(register_15_q), .Q(out_18), .clk(Done));  // open: en, clr
  Register #(.width(32), .trigger("falling")) register_48 (.D(register_16_q), .Q(out_19), .clk(Done));  // open: en, clr
  Register #(.width(32), .trigger("falling")) register_49 (.D(register_17_q), .Q(out_20), .clk(Done));  // open: en, clr
  Register #(.width(32), .trigger("falling")) register_50 (.D(register_18_q), .Q(out_21), .clk(Done));  // open: en, clr
  Register #(.width(32), .trigger("falling")) register_51 (.D(register_19_q), .Q(out_22), .clk(Done));  // open: en, clr
  Register #(.width(32), .trigger("falling")) register_52 (.D(register_20_q), .Q(out_23), .clk(Done));  // open: en, clr
  Register #(.width(32), .trigger("falling")) register_53 (.D(register_21_q), .Q(out_24), .clk(Done));  // open: en, clr
  Register #(.width(32), .trigger("falling")) register_54 (.D(register_22_q), .Q(out_25), .clk(Done));  // open: en, clr
  Register #(.width(32), .trigger("falling")) register_55 (.D(register_23_q), .Q(out_26), .clk(Done));  // open: en, clr
  Register #(.width(32), .trigger("falling")) register_56 (.D(register_24_q), .Q(out_27), .clk(Done));  // open: en, clr
  Register #(.width(32), .trigger("falling")) register_57 (.D(register_25_q), .Q(out_28), .clk(Done));  // open: en, clr
  Register #(.width(32), .trigger("falling")) register_58 (.D(register_26_q), .Q(out_29), .clk(Done));  // open: en, clr
  Register #(.width(32), .trigger("falling")) register_59 (.D(register_27_q), .Q(out_30), .clk(Done));  // open: en, clr
  Register #(.width(32), .trigger("falling")) register_60 (.D(register_28_q), .Q(out_31), .clk(Done));  // open: en, clr
  Register #(.width(32), .trigger("falling")) register_61 (.D(register_29_q), .Q(out_32), .clk(Done));  // open: en, clr
  Register #(.width(32), .trigger("falling")) register_62 (.D(register_30_q), .Q(out_33), .clk(Done));  // open: en, clr
  Register #(.width(32), .trigger("falling")) register_63 (.D(register_31_q), .Q(out_34), .clk(Done));  // open: en, clr
  Register #(.width(32), .trigger("falling")) register_64 (.D(register_32_q), .Q(out_35), .clk(Done));  // open: en, clr
endmodule
