// Logisim project entity_spawner.circ as structural Verilog: 1 circuit, main circuit main
module main (
  input  clk,
  input  r0,
  input  r1,
  input  r2,
  input  r3,
  input  r4,
  input  r5,
  input  r6,
  input  r7,
  input  r8,
  input  r9,
  input  r10,
  input  r11,
  output out0,
  output out1,
  output out2,
  output out3,
  output out4,
  output out5,
  output out6,
  output out7,
  output out8,
  output out9,
  output out10,
  output out11
);

  wire demultiplexer_1_out4, demultiplexer_1_out6, demultiplexer_1_out8, demultiplexer_1_out10,
       demultiplexer_1_out12, demultiplexer_1_out14, demultiplexer_1_out16, demultiplexer_1_out18,
       demultiplexer_1_out20, demultiplexer_1_out22, demultiplexer_1_out24, demultiplexer_1_out26;
  wire [4:0] random_1_out;

  Demultiplexer #(.select(5), .enable("false")) demultiplexer_1 (
    .out4(demultiplexer_1_out4), .out6(demultiplexer_1_out6), .out8(demultiplexer_1_out8),
    .out10(demultiplexer_1_out10), .out12(demultiplexer_1_out12), .out14(demultiplexer_1_out14),
    .out16(demultiplexer_1_out16), .out18(demultiplexer_1_out18), .out20(demultiplexer_1_out20),
    .out22(demultiplexer_1_out22), .out24(demultiplexer_1_out24), .out26(demultiplexer_1_out26), .in(1'b1),
    .sel(random_1_out));  // open: out0, out1, out2, out3, out5, out7, out9, out11, out13, out15, out17, out19, out21, out23, out25, out27, out28, out29, out30, out31
  Random #(.width(5), .seed(35165)) random_1 (.clk(clk), .out(random_1_out));  // open: next, clr
  spawn_register_main main_1 (
    .clk(clk), .spawn0(demultiplexer_1_out4), .spawn1(demultiplexer_1_out6), .spawn2(demultiplexer_1_out8),
    .spawn3(demultiplexer_1_out10), .spawn4(demultiplexer_1_out12), .spawn5(demultiplexer_1_out14),
    .spawn6(demultiplexer_1_out16), .spawn7(demultiplexer_1_out18), .spawn8(demultiplexer_1_out20),
    .spawn9(demultiplexer_1_out22), .spawn10(demultiplexer_1_out24), .spawn11(demultiplexer_1_out26),
    .out0(out0), .r0(r0), .out1(out1), .r1(r1), .out2(out2), .r2(r2), .out3(out3), .r3(r3), .out4(out4),
    .r4(r4), .out5(out5), .r5(r5), .out6(out6), .r6(r6), .out7(out7), .r7(r7), .out8(out8), .r8(r8),
    .out9(out9), .r9(r9), .out10(out10), .r10(r10), .out11(out11), .r11(r11));
endmodule
