// Logisim project game_over_manager.circ as structural Verilog: 1 circuit, main circuit main
module main (
  input  [31:0] normal_led,
  input  [4:0] select,
  input  over,
  output [31:0] led
);

  wire [31:0] rom_1_data;

  ROM #(.addrWidth(5), .dataWidth(32)) rom_1 (.addr(select), .data(rom_1_data));  // open: sel
  Multiplexer #(.width(32), .enable("false")) multiplexer_1 (.in0(normal_led), .in1(rom_1_data), .out(led), .sel(over));

  // Notes on the sheet:
  //   contents of rom_1 (hex, n*v repeats v):
  //   4*0 7c3e00 824100 824100 924100 5c3e00 0 7e7c00 900200 900100 900200 7e7c00 0 fe7f00 404900 204900
  //   404900 fe4100 0 fe7f00 924800 924c00 924a00 823100
endmodule
