// Logisim project keyboard_processor.circ as structural Verilog: 1 circuit, main circuit main
module main (
  input  [6:0] keyboard,
  input  buffer_done,
  output [4:0] out
);

  wire comparator_1_eq, comparator_2_eq, or_1_out;
  wire [4:0] counter_1_q;

  Comparator #(.width(7), .mode("unsigned")) comparator_1 (
    .a(keyboard), .b(7'b1100100), .eq(comparator_1_eq));  // open: gt, lt
  Comparator #(.width(7), .mode("unsigned")) comparator_2 (
    .a(keyboard), .b(7'b1100001), .eq(comparator_2_eq));  // open: gt, lt
  Counter #(.width(5), .max('h1b), .ongoal("stay")) counter_1 (
    .load(comparator_1_eq), .Q(counter_1_q), .clk(or_1_out));  // open: D, count, carry, clr
  or or_1 (or_1_out, comparator_1_eq, comparator_2_eq);
  Register #(.width(5)) register_1 (.D(counter_1_q), .Q(out), .clk(buffer_done));  // open: en, clr

  // Notes on the sheet:
  //   a
  //   d
endmodule
