// Logisim project level_handler.circ as structural Verilog: 1 circuit, main circuit main
module main (
  input  lvl1,
  input  lvl2,
  input  lvl3,
  input  lvl4,
  input  clk,
  input  [15:0] score,
  input  reset,
  output \output ,
  output [7:0] led_lvl
);

  wire and_1_out, and_2_out, and_3_out, and_4_out, and_5_out, and_6_out, and_7_out, comparator_1_lt,
       comparator_2_lt, comparator_3_lt, d_ff_1_q, d_ff_2_q, d_ff_3_q, demultiplexer_1_out0,
       demultiplexer_1_out1, demultiplexer_1_out2, demultiplexer_1_out3, not_1_out, not_2_out, not_3_out,
       or_1_out;
  wire [1:0] counter_1_q;

  Comparator #(.width(16), .mode("unsigned")) comparator_1 (
    .a(score), .b(16'h1c2), .lt(comparator_1_lt));  // open: gt, eq
  Comparator #(.width(16), .mode("unsigned")) comparator_2 (
    .a(score), .b(16'h352), .lt(comparator_2_lt));  // open: gt, eq
  Comparator #(.width(16), .mode("unsigned")) comparator_3 (
    .a(score), .b(16'h5dc), .lt(comparator_3_lt));  // open: gt, eq
  not not_1 (not_1_out, comparator_1_lt);
  not not_2 (not_2_out, comparator_2_lt);
  not not_3 (not_3_out, comparator_3_lt);
  D_Flip_Flop d_ff_1 (.clk(clk), .D(not_1_out), .Q(d_ff_1_q));  // open: Qn, preset, en, reset
  and and_1 (and_1_out, ~d_ff_1_q, not_1_out);  // AND_Gate
  D_Flip_Flop d_ff_2 (.clk(clk), .D(not_2_out), .Q(d_ff_2_q));  // open: Qn, preset, en, reset
  and and_2 (and_2_out, ~d_ff_2_q, not_2_out);  // AND_Gate
  D_Flip_Flop d_ff_3 (.clk(clk), .D(not_3_out), .Q(d_ff_3_q));  // open: Qn, preset, en, reset
  and and_3 (and_3_out, ~d_ff_3_q, not_3_out);  // AND_Gate
  or or_1 (or_1_out, and_1_out, and_2_out, and_3_out);
  Counter #(.width(2), .max('h3)) counter_1 (
    .Q(counter_1_q), .clk(or_1_out), .clr(reset));  // open: load, D, count, carry
  Demultiplexer #(.select(2), .enable("false")) demultiplexer_1 (
    .out0(demultiplexer_1_out0), .out1(demultiplexer_1_out1), .out2(demultiplexer_1_out2),
    .out3(demultiplexer_1_out3), .in(1'b1), .sel(counter_1_q));
  or or_2 (\output , and_5_out, and_4_out, and_7_out, and_6_out);
  and and_4 (and_4_out, demultiplexer_1_out1, lvl2);
  and and_5 (and_5_out, demultiplexer_1_out0, lvl1);
  ROM #(.addrWidth(2)) rom_1 (.addr(counter_1_q), .data(led_lvl));  // open: sel
  and and_6 (and_6_out, demultiplexer_1_out3, lvl4);
  and and_7 (and_7_out, demultiplexer_1_out2, lvl3);

  // Notes on the sheet:
  //   contents of rom_1 (hex, n*v repeats v):
  //   60 da f2 66
endmodule
