// Logisim project rising_edge_detector.circ as structural Verilog: 1 circuit, main circuit main
module main (
  input  clk,
  input  sig,
  output out
);

  wire d_ff_1_q;

  D_Flip_Flop d_ff_1 (.clk(clk), .D(sig), .Q(d_ff_1_q));  // open: Qn, preset, en, reset
  and and_1 (out, ~d_ff_1_q, sig);  // AND_Gate
endmodule
