// Logisim project score_comparation_for_msg.circ as structural Verilog: 1 circuit, main circuit main
module main (
  input  clk,
  input  [15:0] score,
  input  reset,
  output [15:0] out,
  output pulse
);

  wire comparator_1_gt, not_1_out;
  wire [4:0] counter_1_q;

  Counter #(.width(5), .max('h1f)) counter_1 (
    .Q(counter_1_q), .clk(pulse), .clr(reset));  // open: load, D, count, carry
  Multiplexer #(.select(5), .width(16), .enable("false")) multiplexer_1 (
    .in0(16'h12c), .in1(16'h32c), .in2(16'h42c), .in3({16{1'b1}}), .in4({16{1'b1}}), .in5(16'h12c),
    .out(out), .sel(counter_1_q));  // open: in6, in7, in8, in9, in10, in11, in12, in13, in14, in15, in16, in17, in18, in19, in20, in21, in22, in23, in24, in25, in26, in27, in28, in29, in30, in31
  not not_1 (not_1_out, comparator_1_gt);
  Comparator #(.width(16), .mode("unsigned")) comparator_1 (.a(out), .b(score), .gt(comparator_1_gt));  // open: eq, lt
  D_Flip_Flop d_ff_1 (.clk(clk), .D(not_1_out), .Q(pulse));  // open: Qn, preset, en, reset
endmodule
