// Logisim project score_updater.circ as structural Verilog: 1 circuit, main circuit main
module main (
  input  collision__eagle,
  input  collision__student,
  input  clk,
  output [7:0] led_lives,
  output its_over,
  output [23:0] led_students,
  output [31:0] led_score,
  output [15:0] score
);

  wire and_1_out;
  wire [3:0] counter_1_q, divider_2_out;
  wire [9:0] counter_2_q, divider_1_out;
  wire [15:0] counter_3_q;

  Counter #(.width(4), .max('hf), .ongoal("stay")) counter_1 (
    .Q(counter_1_q), .carry(its_over), .clk(collision__eagle));  // open: load, D, count, clr
  Counter #(.width(10), .max('h3ff), .ongoal("stay")) counter_2 (
    .Q(counter_2_q), .clk(collision__student));  // open: load, D, count, carry, clr
  Counter #(.width(16), .max('hffff), .ongoal("stay")) counter_3 (
    .Q(counter_3_q), .clk(and_1_out));  // open: load, D, count, carry, clr
  and and_1 (and_1_out, collision__student, clk);
  Divider #(.width(10)) divider_1 (.a(counter_2_q), .b(10'h2), .out(divider_1_out));  // open: upper, rem
  Multiplier #(.width(16)) multiplier_1 (.a(counter_3_q), .b(16'h2), .out(score));  // open: cin, cout
  Divider #(.width(4)) divider_2 (.a(counter_1_q), .b(4'b0010), .out(divider_2_out));  // open: upper, rem
  ROM #(.addrWidth(4)) rom_1 (.addr(divider_2_out), .data(led_lives));  // open: sel
  ROM #(.addrWidth(10), .dataWidth(24)) rom_2 (.addr(divider_1_out), .data(led_students));  // open: sel
  ROM #(.addrWidth(16), .dataWidth(32)) rom_3 (.addr(score), .data(led_score));  // open: sel

  // Notes on the sheet:
  //   liczy STRACONE zycia
  //   contents of rom_1 (hex, n*v repeats v):
  //   e0 bf b6 66 f2 da 60 fc
  //   contents of rom_2 (hex, n*v repeats v):
  //   fcfcfc fcfc60 fcfcda fcfcf2 fcfc66 fcfcb6 fcfcbf fcfce0 fcfcfe fcfcf7 fc60fc fc6060 fc60da fc60f2
  //   fc6066 fc60b6 fc60bf fc60e0 fc60fe fc60f7 fcdafc fcda60 fcdada fcdaf2 fcda66 fcdab6 fcdabf fcdae0
  //   fcdafe fcdaf7 fcf2fc fcf260 fcf2da fcf2f2 fcf266 fcf2b6 fcf2bf fcf2e0 fcf2fe fcf2f7 fc66fc fc6660
  //   fc66da fc66f2 fc6666 fc66b6 fc66bf fc66e0 fc66fe fc66f7 fcb6fc fcb660 fcb6da fcb6f2 fcb666 fcb6b6
  //   fcb6bf fcb6e0 fcb6fe fcb6f7 fcbffc fcbf60 fcbfda fcbff2 fcbf66 fcbfb6 fcbfbf fcbfe0 fcbffe fcbff7
  //   fce0fc fce060 fce0da fce0f2 fce066 fce0b6 fce0bf fce0e0 fce0fe fce0f7 fcfefc fcfe60 fcfeda fcfef2
  //   fcfe66 fcfeb6 fcfebf fcfee0 fcfefe fcfef7 fcf7fc fcf760 fcf7da fcf7f2 fcf766 fcf7b6 fcf7bf fcf7e0
  //   fcf7fe fcf7f7 60fcfc 60fc60 60fcda 60fcf2 60fc66 60fcb6 60fcbf 60fce0 60fcfe 60fcf7 6060fc 606060
  //   6060da 6060f2 606066 6060b6 6060bf 6060e0 6060fe 6060f7 60dafc 60da60 60dada 60daf2 60da66 60dab6
  //   60dabf 60dae0 60dafe 60daf7 60f2fc 60f260 60f2da 60f2f2 60f266 60f2b6 60f2bf 60f2e0 60f2fe 60f2f7
  //   6066fc 606660 6066da 6066f2 606666 6066b6 6066bf 6066e0 6066fe 6066f7 60b6fc 60b660 60b6da 60b6f2
  //   60b666 60b6b6 60b6bf 60b6e0 60b6fe 60b6f7 60bffc 60bf60 60bfda 60bff2 60bf66 60bfb6 60bfbf 60bfe0
  //   60bffe 60bff7 60e0fc 60e060 60e0da 60e0f2 60e066 60e0b6 60e0bf 60e0e0 60e0fe 60e0f7 60fefc 60fe60
  //   60feda 60fef2 60fe66 60feb6 60febf 60fee0 60fefe 60fef7 60f7fc 60f760 60f7da 60f7f2 60f766 60f7b6
  //   60f7bf 60f7e0 60f7fe 60f7f7 dafcfc dafc60 dafcda dafcf2 dafc66 dafcb6 dafcbf dafce0 dafcfe dafcf7
  //   da60fc da6060 da60da da60f2 da6066 da60b6 da60bf da60e0 da60fe da60f7 dadafc dada60 dadada dadaf2
  //   dada66 dadab6 dadabf dadae0 dadafe dadaf7 daf2fc daf260 daf2da daf2f2 daf266 daf2b6 daf2bf daf2e0
  //   daf2fe daf2f7 da66fc da6660 da66da da66f2 da6666 da66b6 da66bf da66e0 da66fe da66f7 dab6fc dab660
  //   dab6da dab6f2 dab666 dab6b6 dab6bf dab6e0 dab6fe dab6f7 dabffc dabf60 dabfda dabff2 dabf66 dabfb6
  //   dabfbf dabfe0 dabffe dabff7 dae0fc dae060 dae0da dae0f2 dae066 dae0b6 dae0bf dae0e0 dae0fe dae0f7
  //   dafefc dafe60 dafeda dafef2 dafe66 dafeb6 dafebf dafee0 dafefe dafef7 daf7fc daf760 daf7da daf7f2
  //   daf766 daf7b6 daf7bf daf7e0 daf7fe daf7f7 f2fcfc f2fc60 f2fcda f2fcf2 f2fc66 f2fcb6 f2fcbf f2fce0
  //   f2fcfe f2fcf7 f260fc f26060 f260da f260f2 f26066 f260b6 f260bf f260e0 f260fe f260f7 f2dafc f2da60
  //   f2dada f2daf2 f2da66 f2dab6 f2dabf f2dae0 f2dafe f2daf7 f2f2fc f2f260 f2f2da f2f2f2 f2f266 f2f2b6
  //   f2f2bf f2f2e0 f2f2fe f2f2f7 f266fc f26660 f266da f266f2 f26666 f266b6 f266bf f266e0 f266fe f266f7
  //   f2b6fc f2b660 f2b6da f2b6f2 f2b666 f2b6b6 f2b6bf f2b6e0 f2b6fe f2b6f7 f2bffc f2bf60 f2bfda f2bff2
  //   f2bf66 f2bfb6 f2bfbf f2bfe0 f2bffe f2bff7 f2e0fc f2e060 f2e0da f2e0f2 f2e066 f2e0b6 f2e0bf f2e0e0
  //   f2e0fe f2e0f7 f2fefc f2fe60 f2feda f2fef2 f2fe66 f2feb6 f2febf f2fee0 f2fefe f2fef7 f2f7fc f2f760
  //   f2f7da f2f7f2 f2f766 f2f7b6 f2f7bf f2f7e0 f2f7fe f2f7f7 66fcfc 66fc60 66fcda 66fcf2 66fc66 66fcb6
  //   66fcbf 66fce0 66fcfe 66fcf7 6660fc 666060 6660da 6660f2 666066 6660b6 6660bf 6660e0 6660fe 6660f7
  //   66dafc 66da60 66dada 66daf2 66da66 66dab6 66dabf 66dae0 66dafe 66daf7 66f2fc 66f260 66f2da 66f2f2
  //   66f266 66f2b6 66f2bf 66f2e0 66f2fe 66f2f7 6666fc 666660 6666da 6666f2 666666 6666b6 6666bf 6666e0
  //   6666fe 6666f7 66b6fc 66b660 66b6da 66b6f2 66b666 66b6b6 66b6bf 66b6e0 66b6fe 66b6f7 66bffc 66bf60
  //   66bfda 66bff2 66bf66 66bfb6 66bfbf 66bfe0 66bffe 66bff7 66e0fc 66e060 66e0da 66e0f2 66e066 66e0b6
  //   66e0bf 66e0e0 66e0fe 66e0f7 66fefc 66fe60 66feda 66fef2 66fe66 66feb6 66febf 66fee0 66fefe 66fef7
  //   66f7fc 66f760 66f7da 66f7f2 66f766 66f7b6 66f7bf 66f7e0 66f7fe 66f7f7 b6fcfc b6fc60 b6fcda b6fcf2
  //   b6fc66 b6fcb6 b6fcbf b6fce0 b6fcfe b6fcf7 b660fc b66060 b660da b660f2 b66066 b660b6 b660bf b660e0
  //   b660fe b660f7 b6dafc b6da60 b6dada b6daf2 b6da66 b6dab6 b6dabf b6dae0 b6dafe b6daf7 b6f2fc b6f260
  //   b6f2da b6f2f2 b6f266 b6f2b6 b6f2bf b6f2e0 b6f2fe b6f2f7 b666fc b66660 b666da b666f2 b66666 b666b6
  //   b666bf b666e0 b666fe b666f7 b6b6fc b6b660 b6b6da b6b6f2 b6b666 b6b6b6 b6b6bf b6b6e0 b6b6fe b6b6f7
  //   b6bffc b6bf60 b6bfda b6bff2 b6bf66 b6bfb6 b6bfbf b6bfe0 b6bffe b6bff7 b6e0fc b6e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
  //   contents of rom_3 (hex, n*v repeats v):
  //   fcfcfcfc fcfcfc60 fcfcfcda fcfcfcf2 fcfcfc66 fcfcfcb6 fcfcfcbf fcfcfce0 fcfcfcfe fcfcfcf7 fcfc60fc
  //   fcfc6060 fcfc60da fcfc60f2 fcfc6066 fcfc60b6 fcfc60bf fcfc60e0 fcfc60fe fcfc60f7 fcfcdafc fcfcda60
  //   fcfcdada fcfcdaf2 fcfcda66 fcfcdab6 fcfcdabf fcfcdae0 fcfcdafe fcfcdaf7 fcfcf2fc fcfcf260 fcfcf2da
  //   fcfcf2f2 fcfcf266 fcfcf2b6 fcfcf2bf fcfcf2e0 fcfcf2fe fcfcf2f7 fcfc66fc fcfc6660 fcfc66da fcfc66f2
  //   fcfc6666 fcfc66b6 fcfc66bf fcfc66e0 fcfc66fe fcfc66f7 fcfcb6fc fcfcb660 fcfcb6da fcfcb6f2 fcfcb666
  //   fcfcb6b6 fcfcb6bf fcfcb6e0 fcfcb6fe fcfcb6f7 fcfcbffc fcfcbf60 fcfcbfda fcfcbff2 fcfcbf66 fcfcbfb6
  //   fcfcbfbf fcfcbfe0 fcfcbffe fcfcbff7 fcfce0fc fcfce060 fcfce0da fcfce0f2 fcfce066 fcfce0b6 fcfce0bf
  //   fcfce0e0 fcfce0fe fcfce0f7 fcfcfefc fcfcfe60 fcfcfeda fcfcfef2 fcfcfe66 fcfcfeb6 fcfcfebf fcfcfee0
  //   fcfcfefe fcfcfef7 fcfcf7fc fcfcf760 fcfcf7da fcfcf7f2 fcfcf766 fcfcf7b6 fcfcf7bf fcfcf7e0 fcfcf7fe
  //   fcfcf7f7 fc60fcfc fc60fc60 fc60fcda fc60fcf2 fc60fc66 fc60fcb6 fc60fcbf fc60fce0 fc60fcfe fc60fcf7
  //   fc6060fc fc606060 fc6060da fc6060f2 fc606066 fc6060b6 fc6060bf fc6060e0 fc6060fe fc6060f7 fc60dafc
  //   fc60da60 fc60dada fc60daf2 fc60da66 fc60dab6 fc60dabf fc60dae0 fc60dafe fc60daf7 fc60f2fc fc60f260
  //   fc60f2da fc60f2f2 fc60f266 fc60f2b6 fc60f2bf fc60f2e0 fc60f2fe fc60f2f7 fc6066fc fc606660 fc6066da
  //   fc6066f2 fc606666 fc6066b6 fc6066bf fc6066e0 fc6066fe fc6066f7 fc60b6fc fc60b660 fc60b6da fc60b6f2
  //   fc60b666 fc60b6b6 fc60b6bf fc60b6e0 fc60b6fe fc60b6f7 fc60bffc fc60bf60 fc60bfda fc60bff2 fc60bf66
  //   fc60bfb6 fc60bfbf fc60bfe0 fc60bffe fc60bff7 fc60e0fc fc60e060 fc60e0da fc60e0f2 fc60e066 fc60e0b6
  //   fc60e0bf fc60e0e0 fc60e0fe fc60e0f7 fc60fefc fc60fe60 fc60feda fc60fef2 fc60fe66 fc60feb6 fc60febf
  //   fc60fee0 fc60fefe fc60fef7 fc60f7fc fc60f760 fc60f7da fc60f7f2 fc60f766 fc60f7b6 fc60f7bf fc60f7e0
  //   fc60f7fe fc60f7f7 fcdafcfc fcdafc60 fcdafcda fcdafcf2 fcdafc66 fcdafcb6 fcdafcbf fcdafce0 fcdafcfe
  //   fcdafcf7 fcda60fc fcda6060 fcda60da fcda60f2 fcda6066 fcda60b6 fcda60bf fcda60e0 fcda60fe fcda60f7
  //   fcdadafc fcdada60 fcdadada fcdadaf2 fcdada66 fcdadab6 fcdadabf fcdadae0 fcdadafe fcdadaf7 fcdaf2fc
  //   fcdaf260 fcdaf2da fcdaf2f2 fcdaf266 fcdaf2b6 fcdaf2bf fcdaf2e0 fcdaf2fe fcdaf2f7 fcda66fc fcda6660
  //   fcda66da fcda66f2 fcda6666 fcda66b6 fcda66bf fcda66e0 fcda66fe fcda66f7 fcdab6fc fcdab660 fcdab6da
  //   fcdab6f2 fcdab666 fcdab6b6 fcdab6bf fcdab6e0 fcdab6fe fcdab6f7 fcdabffc fcdabf60 fcdabfda fcdabff2
  //   fcdabf66 fcdabfb6 fcdabfbf fcdabfe0 fcdabffe fcdabff7 fcdae0fc fcdae060 fcdae0da fcdae0f2 fcdae066
  //   fcdae0b6 fcdae0bf fcdae0e0 fcdae0fe fcdae0f7 fcdafefc fcdafe60 fcdafeda fcdafef2 fcdafe66 fcdafeb6
  //   fcdafebf fcdafee0 fcdafefe fcdafef7 fcdaf7fc fcdaf760 fcdaf7da fcdaf7f2 fcdaf766 fcdaf7b6 fcdaf7bf
  //   fcdaf7e0 fcdaf7fe fcdaf7f7 fcf2fcfc fcf2fc60 fcf2fcda fcf2fcf2 fcf2fc66 fcf2fcb6 fcf2fcbf fcf2fce0
  //   fcf2fcfe fcf2fcf7 fcf260fc fcf26060 fcf260da fcf260f2 fcf26066 fcf260b6 fcf260bf fcf260e0 fcf260fe
  //   fcf260f7 fcf2dafc fcf2da60 fcf2dada fcf2daf2 fcf2da66 fcf2dab6 fcf2dabf fcf2dae0 fcf2dafe fcf2daf7
  //   fcf2f2fc fcf2f260 fcf2f2da fcf2f2f2 fcf2f266 fcf2f2b6 fcf2f2bf fcf2f2e0 fcf2f2fe fcf2f2f7 fcf266fc
  //   fcf26660 fcf266da fcf266f2 fcf26666 fcf266b6 fcf266bf fcf266e0 fcf266fe fcf266f7 fcf2b6fc fcf2b660
  //   fcf2b6da fcf2b6f2 fcf2b666 fcf2b6b6 fcf2b6bf fcf2b6e0 fcf2b6fe fcf2b6f7 fcf2bffc fcf2bf60 fcf2bfda
  //   fcf2bff2 fcf2bf66 fcf2bfb6 fcf2bfbf fcf2bfe0 fcf2bffe fcf2bff7 fcf2e0fc fcf2e060 fcf2e0da fcf2e0f2
  //   fcf2e066 fcf2e0b6 fcf2e0bf fcf2e0e0 fcf2e0fe fcf2e0f7 fcf2fefc fcf2fe60 fcf2feda fcf2fef2 fcf2fe66
  //   fcf2feb6 fcf2febf fcf2fee0 fcf2fefe fcf2fef7 fcf2f7fc fcf2f760 fcf2f7da fcf2f7f2 fcf2f766 fcf2f7b6
  //   fcf2f7bf fcf2f7e0 fcf2f7fe fcf2f7f7 fc66fcfc fc66fc60 fc66fcda fc66fcf2 fc66fc66 fc66fcb6 fc66fcbf
  //   fc66fce0 fc66fcfe fc66fcf7 fc6660fc fc666060 fc6660da fc6660f2 fc666066 fc6660b6 fc6660bf fc6660e0
  //   fc6660fe fc6660f7 fc66dafc fc66da60 fc66dada fc66daf2 fc66da66 fc66dab6 fc66dabf fc66dae0 fc66dafe
  //   fc66daf7 fc66f2fc fc66f260 fc66f2da fc66f2f2 fc66f266 fc66f2b6 fc66f2bf fc66f2e0 fc66f2fe fc66f2f7
  //   fc6666fc fc666660 fc6666da fc6666f2 fc66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
endmodule
