// Logisim project single_pulse_generator.circ as structural Verilog: 1 circuit, main circuit main
module main (
  input  clock,
  input  trigger,
  output \output 
);

  wire and_1_out, j_k_ff_2_q, j_k_ff_2_qn, not_1_out, not_2_out;

  not not_1 (not_1_out, trigger);
  and and_1 (and_1_out, trigger, j_k_ff_2_qn);
  not not_2 (not_2_out, clock);
  J_K_Flip_Flop j_k_ff_1 (.J(and_1_out), .clk(clock), .K(j_k_ff_2_q), .Q(\output ));  // open: Qn, preset, en, reset
  J_K_Flip_Flop j_k_ff_2 (
    .J(\output ), .clk(not_2_out), .K(not_1_out), .Q(j_k_ff_2_q), .Qn(j_k_ff_2_qn));  // open: preset, en, reset

  // Notes on the sheet:
  //   generator szpilek nie dziala za dobrze jak tick speed jest zbyt duzy
endmodule
