// Logisim project spawn_register.circ as structural Verilog: 1 circuit, main circuit main
module main (
  input  clk,
  input  spawn0,
  input  r0,
  input  spawn1,
  input  r1,
  input  spawn2,
  input  r2,
  input  spawn3,
  input  r3,
  input  spawn4,
  input  r4,
  input  spawn5,
  input  r5,
  input  spawn6,
  input  r6,
  input  spawn7,
  input  r7,
  input  spawn8,
  input  r8,
  input  spawn9,
  input  r9,
  input  spawn10,
  input  r10,
  input  spawn11,
  input  r11,
  output out0,
  output out1,
  output out2,
  output out3,
  output out4,
  output out5,
  output out6,
  output out7,
  output out8,
  output out9,
  output out10,
  output out11
);

  wire d_ff_1_q, d_ff_2_q, d_ff_3_q, d_ff_4_q, d_ff_5_q, d_ff_6_q, d_ff_7_q, d_ff_8_q, d_ff_9_q, d_ff_10_q,
       d_ff_11_q, d_ff_12_q;

  D_Flip_Flop d_ff_1 (.clk(spawn0), .D(1'b1), .Q(d_ff_1_q), .reset(r0));  // open: Qn, preset, en
  D_Flip_Flop d_ff_2 (.clk(spawn1), .D(1'b1), .Q(d_ff_2_q), .reset(r1));  // open: Qn, preset, en
  D_Flip_Flop d_ff_3 (.clk(spawn2), .D(1'b1), .Q(d_ff_3_q), .reset(r2));  // open: Qn, preset, en
  D_Flip_Flop d_ff_4 (.clk(spawn3), .D(1'b1), .Q(d_ff_4_q), .reset(r3));  // open: Qn, preset, en
  D_Flip_Flop d_ff_5 (.clk(spawn4), .D(1'b1), .Q(d_ff_5_q), .reset(r4));  // open: Qn, preset, en
  D_Flip_Flop d_ff_6 (.clk(spawn5), .D(1'b1), .Q(d_ff_6_q), .reset(r5));  // open: Qn, preset, en
  D_Flip_Flop d_ff_7 (.clk(spawn6), .D(1'b1), .Q(d_ff_7_q), .reset(r6));  // open: Qn, preset, en
  D_Flip_Flop d_ff_8 (.clk(spawn7), .D(1'b1), .Q(d_ff_8_q), .reset(r7));  // open: Qn, preset, en
  D_Flip_Flop d_ff_9 (.clk(spawn8), .D(1'b1), .Q(d_ff_9_q), .reset(r8));  // open: Qn, preset, en
  D_Flip_Flop d_ff_10 (.clk(spawn9), .D(1'b1), .Q(d_ff_10_q), .reset(r9));  // open: Qn, preset, en
  D_Flip_Flop d_ff_11 (.clk(spawn10), .D(1'b1), .Q(d_ff_11_q), .reset(r10));  // open: Qn, preset, en
  D_Flip_Flop d_ff_12 (.clk(spawn11), .D(1'b1), .Q(d_ff_12_q), .reset(r11));  // open: Qn, preset, en
  rising_edge_detector_main main_1 (.clk(clk), .sig(d_ff_1_q), .out(out0));
  rising_edge_detector_main main_2 (.clk(clk), .sig(d_ff_2_q), .out(out1));
  rising_edge_detector_main main_3 (.clk(clk), .sig(d_ff_3_q), .out(out2));
  rising_edge_detector_main main_4 (.clk(clk), .sig(d_ff_4_q), .out(out3));
  rising_edge_detector_main main_5 (.clk(clk), .sig(d_ff_5_q), .out(out4));
  rising_edge_detector_main main_6 (.clk(clk), .sig(d_ff_6_q), .out(out5));
  rising_edge_detector_main main_7 (.clk(clk), .sig(d_ff_7_q), .out(out6));
  rising_edge_detector_main main_8 (.clk(clk), .sig(d_ff_8_q), .out(out7));
  rising_edge_detector_main main_9 (.clk(clk), .sig(d_ff_9_q), .out(out8));
  rising_edge_detector_main main_10 (.clk(clk), .sig(d_ff_10_q), .out(out9));
  rising_edge_detector_main main_11 (.clk(clk), .sig(d_ff_11_q), .out(out10));
  rising_edge_detector_main main_12 (.clk(clk), .sig(d_ff_12_q), .out(out11));
endmodule
