// Logisim project student_catcher.circ as structural Verilog: 1 circuit, main circuit main
module main (
  input  [31:0] student,
  input  [31:0] profesor,
  output catch
);

  wire [31:0] and_1_out;

  assign and_1_out = student & profesor;  // AND_Gate and_1, 32 bits wide
  or or_1 (catch, and_1_out[16], and_1_out[31], and_1_out[30], and_1_out[29], and_1_out[28], and_1_out[27], and_1_out[26], and_1_out[25], and_1_out[24], and_1_out[23], and_1_out[22], and_1_out[21], and_1_out[20], and_1_out[19], and_1_out[18], and_1_out[17], and_1_out[15], and_1_out[14], and_1_out[13], and_1_out[12], and_1_out[11], and_1_out[10], and_1_out[9], and_1_out[8], and_1_out[7], and_1_out[6], and_1_out[5], and_1_out[4], and_1_out[3], and_1_out[2], and_1_out[1], and_1_out[0]);
endmodule
