// Logisim project student_drop.circ as structural Verilog: 1 circuit, main circuit main
module main (
  input  [31:0] \input ,
  input  catch,
  input  send,
  input  clk,
  output [31:0] \output ,
  output gone
);

  wire and_1_out, and_3_out, and_4_out, and_5_out, and_6_out, d_ff_1_q, d_ff_2_q, d_ff_3_q, nand_1_out,
       not_1_out, not_2_out, or_1_out, or_2_out, or_3_out, or_4_out, or_5_out, or_6_out;
  wire [4:0] counter_1_q, counter_2_q, counter_3_q;
  wire [31:0] and_2_out, multiplexer_1_out, shifter_1_out;

  not not_1 (not_1_out, clk);
  D_Flip_Flop d_ff_1 (.clk(not_1_out), .D(1'b1), .Q(d_ff_1_q));  // open: Qn, preset, en, reset
  D_Flip_Flop d_ff_2 (.clk(not_1_out), .D(d_ff_1_q), .Q(d_ff_2_q));  // open: Qn, preset, en, reset
  and and_1 (and_1_out, ~d_ff_2_q, d_ff_1_q);  // AND_Gate
  Multiplexer #(.width(32), .enable("false")) multiplexer_1 (
    .in0({32{1'b0}}), .in1({32{1'b1}}), .out(multiplexer_1_out), .sel(nand_1_out));
  assign and_2_out = \input  & multiplexer_1_out;  // AND_Gate and_2, 32 bits wide
  Counter #(.width(5), .max('h5)) counter_1 (
    .load(1'b1), .Q(counter_1_q), .clk(and_3_out));  // open: D, count, carry, clr
  and and_3 (and_3_out, or_1_out, clk);
  or or_1 (or_1_out, send, or_4_out);
  Counter #(.width(5), .max('h6)) counter_2 (
    .load(1'b1), .Q(counter_2_q), .clk(and_4_out));  // open: D, count, carry, clr
  and and_4 (and_4_out, or_2_out, clk);
  or or_2 (or_2_out, send, or_5_out);
  Shifter #(.width(32)) shifter_1 (.in(and_2_out), .\dist (counter_1_q), .out(shifter_1_out));
  or or_3 (or_3_out, and_1_out, catch);
  or or_4 (or_4_out, counter_1_q[0], counter_1_q[1], counter_1_q[2], counter_1_q[3], counter_1_q[4]);
  or or_5 (or_5_out, counter_2_q[0], counter_2_q[1], counter_2_q[2], counter_2_q[3], counter_2_q[4]);
  not not_2 (not_2_out, or_3_out);
  and and_5 (and_5_out, ~or_5_out, clk);  // AND_Gate
  Shifter #(.width(32), .shift("lr")) shifter_2 (.in(shifter_1_out), .\dist (counter_3_q), .out(\output ));
  Counter #(.width(5), .max('h1f)) counter_3 (
    .load(or_3_out), .D({5{1'b1}}), .count(not_2_out), .Q(counter_3_q), .clk(or_6_out));  // open: carry, clr
  or or_6 (or_6_out, or_3_out, send, and_6_out);
  and and_6 (and_6_out, and_5_out, nand_1_out);
  nand nand_1 (nand_1_out, counter_3_q[4], counter_3_q[3], counter_3_q[2], counter_3_q[1], counter_3_q[0]);
  D_Flip_Flop d_ff_3 (.clk(clk), .D(nand_1_out), .Q(d_ff_3_q));  // open: Qn, preset, en, reset
  and and_7 (gone, d_ff_3_q, ~nand_1_out);  // AND_Gate

  // Notes on the sheet:
  //   w gore
  //   w dol
endmodule
