// Logisim project SymulatorPeofesora.circ as structural Verilog: 1 circuit, main circuit main
module main (
  input  in_1,
  input  in_2
);

  wire clock_1_out, main_1_output;
  wire [6:0] main_2_out_4;

  Clock clock_1 (.out(clock_1_out));
  single_pulse_generator_main main_1 (.trigger(in_1), .\output (main_1_output), .clock(clock_1_out));
  ROM_message_spitter_main main_2 (.clock(clock_1_out), .out_4(main_2_out_4), .reset(in_2), .trigger(main_1_output));
  TTY #(.rows(1), .cols(110)) tty_1 (.data(main_2_out_4), .clk(clock_1_out), .clr(main_1_output));  // open: we
endmodule
